# Fritzing sketch SendReceive (saved by Fritzing 0.9.3b)
breadboards: 1

parts:
  U1 = NodeMCU V1.0
  R1 = Resistor [tolerance=±5% resistance=220 package=THT]
  S1 = Pushbutton [package="[SMD]"]
  LED1 = LEDs [package=led10mm]
  R2 = Resistor [tolerance=±5% resistance=10k package=THT]

nets:
  N1: U1.3V3, S1.Pin_3, S1.Pin_4
  N2: U1.GND, LED1.C, R2.Pin_1
  N3: U1.D5, R1.Pin_1
  N4: U1.D6, S1.Pin_1, S1.Pin_2, R2.Pin_0
  N5: R1.Pin_0, LED1.A

custom parts:
  NodeMCU V1.0: ESP8266 based NodeMCU
